# Fritzing sketch wheelChair (saved by Fritzing 0.9.3b)
breadboards: 1

parts:
  Part1 = Arduino Uno (Rev3)
  M1 = DC Motor
  M2 = DC Motor
  hc-sr1 = hc-sr04
  Part2 = Bluetooth HC-05 Macho
  S1 = H-Bridge with L298N
  BAT1 = Battery Holders [package=lipo-1100mAh]  # not connected
  LED2 = LED - 5mm [color="Green (570nm)" package="5 mm [THT]"]

nets:
  N1: Part1.D8, S1.IN1
  N2: Part1.D9_PWM, S1.IN2
  N3: Part1.D10_PWM/SS, S1.IN3
  N4: Part1.D11_PWM/MOSI, S1.IN4
  N5: Part1.D12/MISO, hc-sr1.Trig
  N6: Part1.D13/SCK, hc-sr1.Echo
  GND: Part1.GND, hc-sr1.GND, Part2.GND, S1.GND, LED2.cathode
  N7: Part1.D0/RX, Part2.TXD
  N8: Part1.D1/TX, Part2.RXD
  N9: Part1.D7, LED2.anode
  VCC: Part1.5V, hc-sr1.VCC, Part2.VCC
  VIN: Part1.VIN, S1.5V
  N10: M1.pin_1, S1.M1-02
  N11: M1.pin_2, S1.M1-01
  N12: M2.pin_1, S1.M2-02
  N13: M2.pin_2, S1.M2-01

notes:
  Right Motor
  Left Motor
  Arduino
  Motor Driver
  Lipo Battery
  Bluetooth Module
  Ultrasonic Sensor
  Breadboard
  LED

custom parts:
  H-Bridge with L298N: h-bridge
